// Logisim project cpu_benchmark.circ as structural Verilog: 6 circuits, main circuit cpu
module cpu (
);

  wire alu_1_equal, controller_1_out_6, controller_1_out_8, controller_1_out_9, controller_1_out_11,
       controller_1_out_12, controller_1_out_13, controller_1_out_14, controller_1_out_15, RST,
       syscall_1_out_6, T, undriven;
  wire [1:0] controller_1_out_4, controller_1_out_7, controller_1_out_10;
  wire [2:0] controller_1_out_5;
  wire [3:0] controller_1_out_3;
  wire [4:0] multiplexer_3_out, multiplexer_4_out;
  wire [7:0] multiplexer_5_out;
  wire [23:0] pc_1_out_12, \总周期数 , \无条件分支指令数 , \有条件分支成功跳转 , \有条件分支指令数 ;
  wire [31:0] adder_1_out, alu_1_result, alui_1_out_7, alui_1_out_8, mips_ram_1_p7, multiplexer_6_out,
       pc_1_out_11, registerfile_1_p5, registerfile_1_p6, rom_1_data, shifter_1_out, SyscallOut;

  Button \u_总复位  (.out(RST));
  Clock clock_1 (.out(T));
  PC pc_1 (
    .in_1(registerfile_1_p5), .in_2(rom_1_data[25:0]), .in_3(rom_1_data[15:0]), .in_4(controller_1_out_10),
    .in_5(alu_1_equal), .in_6(RST), .in_7(syscall_1_out_6), .in_8(T), .in_9(controller_1_out_11),
    .out_11(pc_1_out_11), .out_12(pc_1_out_12), .out_13(\总周期数 ), .out_14(\无条件分支指令数 ), .out_15(\有条件分支指令数 ),
    .out_16(\有条件分支成功跳转 ), .in_10(controller_1_out_15));
  Controller controller_1 (
    .in_1(rom_1_data[31:26]), .in_2(rom_1_data[5:0]), .out_9(controller_1_out_9), .out_7(controller_1_out_7),
    .out_3(controller_1_out_3), .out_6(controller_1_out_6), .out_4(controller_1_out_4),
    .out_5(controller_1_out_5), .out_8(controller_1_out_8), .out_10(controller_1_out_10),
    .out_11(controller_1_out_11), .out_14(controller_1_out_14), .out_12(controller_1_out_12),
    .out_13(controller_1_out_13), .out_15(controller_1_out_15));
  Hex_Digit_Display hex_digit_display_1 (.value(SyscallOut[31:28]));  // open: dp
  Hex_Digit_Display hex_digit_display_2 (.value(SyscallOut[27:24]));  // open: dp
  ROM #(.addrWidth(24), .dataWidth(32)) rom_1 (.addr(pc_1_out_12), .data(rom_1_data));  // open: sel
  Hex_Digit_Display hex_digit_display_3 (.value(SyscallOut[19:16]));  // open: dp
  Hex_Digit_Display hex_digit_display_4 (.value(SyscallOut[23:20]));  // open: dp
  Multiplexer #(.width(32)) multiplexer_1 (
    .in0(multiplexer_6_out), .in1(alu_1_result), .sel(controller_1_out_8));  // open: out, en
  Hex_Digit_Display hex_digit_display_5 (.value(SyscallOut[11:8]));  // open: dp
  Hex_Digit_Display hex_digit_display_6 (.value(SyscallOut[15:12]));  // open: dp
  Multiplexer #(.select(2), .width(5)) multiplexer_2 (
    .in0(rom_1_data[15:11]), .in2(rom_1_data[20:16]), .in3({5{1'b1}}), .sel(controller_1_out_7));  // open: in1, out, en
  Multiplexer #(.width(5)) multiplexer_3 (
    .in0(rom_1_data[20:16]), .in1(5'b00100), .out(multiplexer_3_out), .sel(controller_1_out_12), .en(undriven));
  Multiplexer #(.width(5)) multiplexer_4 (
    .in0(rom_1_data[25:21]), .in1(5'b00010), .out(multiplexer_4_out), .sel(controller_1_out_12), .en(undriven));
  Hex_Digit_Display hex_digit_display_7 (.value(SyscallOut[3:0]));  // open: dp
  Hex_Digit_Display hex_digit_display_8 (.value(SyscallOut[7:4]));  // open: dp
  // RegisterFile registerfile_1: pin names not known; wires that end beside it: T, controller_1_out_6, multiplexer_4_out, multiplexer_3_out, registerfile_1_p5, registerfile_1_p6
  // Probe on pc_1_out_11
  Syscall syscall_1 (
    .in_1(registerfile_1_p5), .in_2(registerfile_1_p6), .in_3(controller_1_out_13), .in_4(T), .in_5(RST),
    .out_6(syscall_1_out_6), .out_7(SyscallOut));
  AluI alui_1 (
    .in_3(rom_1_data), .in_1(controller_1_out_4), .in_2(controller_1_out_5), .in_4(registerfile_1_p5),
    .in_5(registerfile_1_p6), .in_6(pc_1_out_11), .out_7(alui_1_out_7), .out_8(alui_1_out_8));
  Adder #(.width(32)) adder_1 (
    .a(registerfile_1_p5), .b({{16{1'b0}}, rom_1_data[15:0]}), .out(adder_1_out));  // open: cin, cout
  Alu alu_1 (
    .X(alui_1_out_7), .Y(alui_1_out_8), .AluOP(controller_1_out_3), .Equal(alu_1_equal), .Result(alu_1_result));  // open: Signed_Overflow, UnSigned_Overflow, Result_2
  // Probe on \总周期数 
  // Probe on \无条件分支指令数 
  // Probe on \有条件分支指令数 
  // Probe on \有条件分支成功跳转 
  Shifter #(.width(32), .shift("lr")) shifter_1 (.in(adder_1_out), .\dist (5'b00010), .out(shifter_1_out));
  Multiplexer #(.select(2), .width(8)) multiplexer_5 (
    .in0(mips_ram_1_p7[7:0]), .in1(mips_ram_1_p7[15:8]), .in2(mips_ram_1_p7[23:16]),
    .in3(mips_ram_1_p7[31:24]), .out(multiplexer_5_out), .sel(adder_1_out[1:0]));  // open: en
  Multiplexer #(.width(32)) multiplexer_6 (
    .in0({{24{1'b0}}, multiplexer_5_out}), .in1(mips_ram_1_p7), .out(multiplexer_6_out),
    .sel(controller_1_out_14));  // open: en
  // MIPS_RAM mips_ram_1: pin names not known; wires that end beside it: shifter_1_out[23:0], registerfile_1_p6, controller_1_out_9, T, 1'b1, RST, mips_ram_1_p7

  // Notes on the sheet:
  //   指令存储器
  //   数码管输出应该用寄存器锁存，否则显示数据只能一闪而过
  //   contents of rom_1 (hex, n*v repeats v):
  //   20110001 8000c05 20110001 20120002 20130003 8000c09 20110001 20120002 20130003 8000c0d 20110001
  //   20120002 20130003 8000c11 20110001 20120002 20130003 c000cb8 20100001 20110001 118fc0 112020
  //   20020022 c 118882 12200001 8000c15 112020 20020022 c 20110001 118880 112020 20020022 c 12200001
  //   8000c1f 20110001 118fc0 112020 20020022 c 1188c3 112020 20020022 c 118903 112020 20020022 c 118903
  //   112020 20020022 c 118903 112020 20020022 c 118903 112020 20020022 c 118903 112020 20020022 c 118903
  //   112020 20020022 c 118903 112020 20020022 c 20100001 109fc0 139fc3 8021 2012000c 24160003 26100001
  //   3210000f 20080008 20090001 139900 2709825 132020 20020022 c 1094022 1500fff9 22100001 2018000f
  //   2188024 108700 20080008 20090001 139902 2709825 132021 20020022 c 1094022 1500fff9 108702 2c9b022
  //   12c00001 8000c50 4020 1084027 84400 3508ffff 82021 20020022 c 2010ffff 20110000 ae300000 22100001
  //   22310004 ae300000 22100001 22310004 ae300000 22100001 22310004 ae300000 22100001 22310004 ae300000
  //   22100001 22310004 ae300000 22100001 22310004 ae300000 22100001 22310004 ae300000 22100001 22310004
  //   ae300000 22100001 22310004 ae300000 22100001 22310004 ae300000 22100001 22310004 ae300000 22100001
  //   22310004 ae300000 22100001 22310004 ae300000 22100001 22310004 ae300000 22100001 22310004 ae300000
  //   22100001 22310004 22100001 8020 2011003c 8e130000 8e340000 274402a 11000002 ae330000 ae140000
  //   2231fffc 1611fff8 102020 20020022 c 22100004 2011003c 1611fff2 2002000a c 20100000 22100001 102020
  //   20020022 c 22100002 102020 20020022 c 22100003 102020 20020022 c 22100004 102020 20020022 c 22100005
  //   102020 20020022 c 22100006 102020 20020022 c 22100007 102020 20020022 c 22100008 102020 20020022
  //   20020022 c 3e00008
  //   可以通过项目增加Logisim库的方式将前几次实验完成的电路作为子电路引入到本电路中使用
  //   rD
  //   寄存器文件
  //   rT
  //   rS
  //   rT
  //   数码管输出
  //   总复位信号应将除ROM以外所有存储组件全部清零
  //   $rS
  //   $rT
  //   Immi
  //   运行内存
endmodule

module Controller (
  input  [5:0] in_1,
  input  [5:0] in_2,
  output [3:0] out_3,
  output [1:0] out_4,
  output [2:0] out_5,
  output out_6,
  output [1:0] out_7,
  output out_8,
  output out_9,
  output [1:0] out_10,
  output out_11,
  output out_12,
  output out_13,
  output out_14,
  output out_15
);

  wire add, addi, addiu, addu, \and , and_1_out, and_2_out, and_3_out, and_4_out, and_5_out, and_6_out,
       and_7_out, and_11_out, and_12_out, andi, beq, bltz_t, bne, j_t, jal, jr, lbu, lw, \nor , Op__0, \or ,
       or_1_out, or_2_out, or_3_out, or_6_out, or_7_out, or_8_out, or_9_out, or_10_out, or_11_out, ori,
       priority_encoder_2_p4, priority_encoder_2_p5, sll, slt, slti, sltiu, sltu, sra, srl, srlv, sub,
       syscall;
  wire [3:0] priority_encoder_1_out, priority_encoder_2_p1;

  Comparator #(.width(6)) comparator_1 (.a(in_1), .b({6{1'b0}}), .eq(Op__0));  // open: gt, lt
  Comparator #(.width(6)) comparator_2 (.a(in_1), .b(6'b000100), .eq(beq));  // open: gt, lt
  Comparator #(.width(6)) comparator_3 (.a(in_1), .b(6'b000101), .eq(bne));  // open: gt, lt
  Comparator #(.width(6)) comparator_4 (.a(in_1), .b(6'b001010), .eq(slti));  // open: gt, lt
  Comparator #(.width(6)) comparator_5 (.a(in_1), .b(6'b001101), .eq(ori));  // open: gt, lt
  Comparator #(.width(6)) comparator_6 (.a(in_1), .b(6'b001100), .eq(andi));  // open: gt, lt
  Comparator #(.width(6)) comparator_7 (.a(in_1), .b(6'b001001), .eq(addiu));  // open: gt, lt
  Comparator #(.width(6)) comparator_8 (.a(in_1), .b(6'b001000), .eq(addi));  // open: gt, lt
  Comparator #(.width(6)) comparator_9 (.a(in_1), .b(6'b000010), .eq(j_t));  // open: gt, lt
  or or_1 (or_1_out, bltz_t, slti);
  or or_2 (or_2_out, bne, beq);
  Comparator #(.width(6)) comparator_10 (.a(in_1), .b(6'b101011), .eq(out_9));  // open: gt, lt
  Comparator #(.width(6)) comparator_11 (.a(in_1), .b(6'b100011), .eq(lw));  // open: gt, lt
  Comparator #(.width(6)) comparator_12 (.a(in_1), .b(6'b000011), .eq(jal));  // open: gt, lt
  Comparator #(.width(6)) comparator_13 (.a(in_2), .b(6'b101011), .eq(sltu));  // open: gt, lt
  Comparator #(.width(6)) comparator_14 (.a(in_2), .b(6'b101010), .eq(slt));  // open: gt, lt
  Comparator #(.width(6)) comparator_15 (.a(in_2), .b(6'b100111), .eq(\nor ));  // open: gt, lt
  Comparator #(.width(6)) comparator_16 (.a(in_2), .b(6'b100101), .eq(\or ));  // open: gt, lt
  Comparator #(.width(6)) comparator_17 (.a(in_2), .b(6'b100100), .eq(\and ));  // open: gt, lt
  or or_3 (or_3_out, jal, addi, lw, out_9, addiu, lbu);
  Priority_Encoder #(.select(4)) priority_encoder_1 (
    .in5(or_3_out), .in7(andi), .in8(ori), .in11(or_1_out), .in12(sltiu), .in14(or_2_out),
    .out(priority_encoder_1_out));  // open: in0, in1, in2, in3, in4, in6, in9, in10, in13, in15, gs, en_out, en_in
  Comparator #(.width(6)) comparator_18 (.a(in_2), .b(6'b100010), .eq(sub));  // open: gt, lt
  Comparator #(.width(6)) comparator_19 (.a(in_2), .b(6'b100001), .eq(addu));  // open: gt, lt
  Comparator #(.width(6)) comparator_20 (.a(in_2), .b(6'b100000), .eq(add));  // open: gt, lt
  Comparator #(.width(6)) comparator_21 (.a(in_2), .b(6'b001100), .eq(syscall));  // open: gt, lt
  Comparator #(.width(6)) comparator_22 (.a(in_2), .b(6'b001000), .eq(jr));  // open: gt, lt
  Comparator #(.width(6)) comparator_23 (.a(in_2), .b(6'b000011), .eq(sra));  // open: gt, lt
  Comparator #(.width(6)) comparator_24 (.a(in_2), .b(6'b000010), .eq(srl));  // open: gt, lt
  Comparator #(.width(6)) comparator_25 (.a(in_2), .b({6{1'b0}}), .eq(sll));  // open: gt, lt
  Multiplexer #(.width(4)) multiplexer_1 (
    .in0(priority_encoder_1_out), .in1(priority_encoder_2_p1), .out(out_3), .sel(Op__0));  // open: en
  // Priority_Encoder #(.select(4)) priority_encoder_2: pin names not known; wires that end beside it: priority_encoder_2_p1, sll, sra, priority_encoder_2_p4, priority_encoder_2_p5, sub, \and , \or , \nor , slt, sltu
  or or_4 (priority_encoder_2_p5, add, addu);
  Multiplexer #(.select(2), .width(2)) multiplexer_2 (
    .in0(2'b10), .in1(2'b11), .in2(2'b00), .in3(2'b00), .out(out_7), .sel({Op__0, jal}));  // open: en
  or or_5 (priority_encoder_2_p4, srl, srlv);
  or or_6 (or_6_out, addiu, lw, addi, jal, slti, ori, andi, lbu, sltiu);
  or or_7 (or_7_out, \nor , sub, \or , \and , slt, add, sra, addu, srl, sltu, sll, srlv);
  Multiplexer multiplexer_3 (.in0(or_6_out), .in1(or_7_out), .out(out_6), .sel(Op__0));  // open: en
  and and_1 (and_1_out, Op__0, jr);
  and and_2 (and_2_out, ~Op__0, beq);  // AND_Gate
  and and_3 (and_3_out, ~Op__0, bne);  // AND_Gate
  or or_8 (or_8_out, sra, srl, sll, srlv);
  or or_9 (or_9_out, slti, sltiu, ori, lw, andi, out_9, lbu, addiu, addi);
  Comparator #(.width(6)) comparator_26 (.a(in_1), .b(6'b000001), .eq(bltz_t));  // open: gt, lt
  Comparator #(.width(6)) comparator_27 (.a(in_1), .b(6'b001011), .eq(sltiu));  // open: gt, lt
  or or_10 (or_10_out, jal, j_t);
  Priority_Encoder #(.select(2)) priority_encoder_3 (
    .in0(1'b1), .in1(and_1_out), .in2(and_2_out), .in3(and_3_out), .out(out_10));  // open: gs, en_out, en_in
  and and_4 (and_4_out, Op__0, or_8_out);
  and and_5 (and_5_out, jal, ~Op__0);  // AND_Gate
  and and_6 (and_6_out, ~Op__0, or_9_out);  // AND_Gate
  and and_7 (and_7_out, srlv, Op__0);
  and and_8 (out_11, or_10_out, ~Op__0);  // AND_Gate
  or or_11 (or_11_out, lbu, lw);
  Priority_Encoder #(.select(2)) priority_encoder_4 (
    .in0(1'b1), .in1(and_4_out), .in2(and_5_out), .out(out_4));  // open: in3, gs, en_out, en_in
  Priority_Encoder priority_encoder_5 (
    .in0(1'b1), .in1(and_4_out), .in2(and_6_out), .in3(and_5_out), .in4(and_7_out), .out(out_5));  // open: in5, in6, in7, en_in, gs, en_out
  Comparator #(.width(6)) comparator_28 (.a(in_1), .b(6'b100100), .eq(lbu));  // open: gt, lt
  Comparator #(.width(6)) comparator_29 (.a(in_2), .b(6'b000110), .eq(srlv));  // open: gt, lt
  and and_9 (out_15, bltz_t, ~Op__0);  // AND_Gate
  and and_10 (out_12, syscall, Op__0);
  not not_1 (out_14, and_11_out);
  and and_11 (and_11_out, lbu, ~Op__0);  // AND_Gate
  not not_2 (out_8, and_12_out);
  and and_12 (and_12_out, or_11_out, ~Op__0);  // AND_Gate
  Decoder #(.select(5)) decoder_1 ();  // open: out0, out1, out2, out3, out4, out5, out6, out7, out8, out9, out10, out11, out12, out13, out14, out15, out16, out17, out18, out19, out20, out21, out22, out23, out24, out25, out26, out27, out28, out29, out30, out31, sel, en
  Decoder #(.select(5)) decoder_2 ();  // open: out0, out1, out2, out3, out4, out5, out6, out7, out8, out9, out10, out11, out12, out13, out14, out15, out16, out17, out18, out19, out20, out21, out22, out23, out24, out25, out26, out27, out28, out29, out30, out31, sel, en
  Decoder #(.select(5)) decoder_3 ();  // open: out0, out1, out2, out3, out4, out5, out6, out7, out8, out9, out10, out11, out12, out13, out14, out15, out16, out17, out18, out19, out20, out21, out22, out23, out24, out25, out26, out27, out28, out29, out30, out31, sel, en
  Decoder #(.select(5)) decoder_4 ();  // open: out0, out1, out2, out3, out4, out5, out6, out7, out8, out9, out10, out11, out12, out13, out14, out15, out16, out17, out18, out19, out20, out21, out22, out23, out24, out25, out26, out27, out28, out29, out30, out31, sel, en

  assign out_13 = out_12;

  // Other names for the same wires on the sheet: AluOp[3:0] = out_3; AluX[1:0] = out_4; AluY[2:0] = out_5;
  //   BLTZ = out_15; J = out_11; nLBU = out_14; Op[5:0] = in_1; PCW[1:0] = out_10; rW = out_8; rW_t[1:0] = out_7;
  //   rWE = out_6; Sp[5:0] = in_2; MemW = out_9; sw = out_9; Sys = out_12

  // Notes on the sheet:
  //   Instructions
  //   Reg Write Dst
  //   O->rD
  //   2->rT
  //   3->$31
  //   Alu Operator
  //   reg Write Enable
  //   RAM Write
  //   Branching
  //   0->PC++
  //   1->$rS
  //   2->beq
  //   3->bne
  //   J/JAL
  //   CCMB
  //   lbtz(CCMB)
  //   Syscall
  //   lbu(CCMB)
  //   Reg Write Src
  //   0->MemO
  //   1->AluR
  //   Alu Input
  //   0->rS(default)
  //   1->rT
  //   2->PC
  //   0->rT(default)
  //   1->sA
  //   2->Immi
  //   3->4
  //   4->rS(CCMB)
endmodule

module Alu (
  input  [31:0] X,
  input  [31:0] Y,
  input  [3:0] AluOP,
  output Signed_Overflow,
  output UnSigned_Overflow,
  output Equal,
  output [31:0] Result,
  output [31:0] Result_2
);

  wire OF1, OF2, UOF1, UOF2, xnor_1_out, xor_1_out, xor_2_out, xor_3_out;
  wire [0:0] R12, R13;
  wire [31:0] R1, R2, R3, R4, R5, R6, R7, R8, R9, R10, R11, R21, R22;

  // Probe on X
  // Probe on X
  // Probe on Y
  // Probe on Y
  Shifter #(.width(32)) shifter_1 (.in(X), .\dist (Y[4:0]), .out(R1));
  Shifter #(.width(32), .shift("ar")) shifter_2 (.in(X), .\dist (Y[4:0]), .out(R2));
  Shifter #(.width(32), .shift("lr")) shifter_3 (.in(X), .\dist (Y[4:0]), .out(R3));
  Multiplier #(.width(32)) multiplier_1 (.a(X), .b(Y), .out(R4), .cout(R21));  // open: cin
  Divider #(.width(32)) divider_1 (.a(X), .b(Y), .out(R5), .rem(R22));  // open: upper
  xnor xnor_1 (xnor_1_out, X[31], Y[31]);
  xor xor_1 (xor_1_out, Y[31], X[31]);
  // Probe on AluOP
  Adder #(.width(32)) adder_1 (.a(X), .b(Y), .out(R6), .cin(1'b0), .cout(UOF1));
  xor xor_2 (xor_2_out, Y[31], R6[31]);
  and and_1 (OF1, xnor_1_out, xor_2_out);
  Subtractor #(.width(32)) subtractor_1 (.a(X), .b(Y), .out(R7), .bin(1'b0), .bout(UOF2));
  xor xor_3 (xor_3_out, X[31], R7[31]);
  and and_2 (OF2, xor_1_out, xor_3_out);
  // Probe on Result
  // Probe on Result
  assign R8 = X & Y;  // AND_Gate and_3, 32 bits wide
  assign R9 = X | Y;  // OR_Gate or_1, 32 bits wide
  assign R10 = X ^ Y;  // XOR_Gate xor_4, 32 bits wide
  assign R11 = ~(X | Y);  // NOR_Gate nor_1, 32 bits wide
  Comparator #(.width(32)) comparator_1 (.a(X), .b(Y), .eq(Equal), .lt(R12[0]));  // open: gt
  Comparator #(.width(32), .mode("unsigned")) comparator_2 (.a(X), .b(Y), .lt(R13[0]));  // open: gt, eq
  // Probe on Result_2
  Multiplexer #(.select(4), .width(32)) multiplexer_1 (
    .in0(R1), .in1(R2), .in2(R3), .in3(R4), .in4(R5), .in5(R6), .in6(R7), .in7(R8), .in8(R9), .in9(R10),
    .in10(R11), .in11({{31{1'b0}}, R12[0]}), .in12({{31{1'b0}}, R13[0]}), .in13({32{1'b0}}),
    .in14({32{1'b0}}), .in15({32{1'b0}}), .out(Result), .sel(AluOP));  // open: en
  Multiplexer #(.select(4)) multiplexer_2 (
    .in0(1'b0), .in1(1'b0), .in2(1'b0), .in3(1'b0), .in4(1'b0), .in5(UOF1), .in6(UOF2), .in7(1'b0),
    .in8(1'b0), .in9(1'b0), .in10(1'b0), .in11(1'b0), .in12(1'b0), .in13(1'b0), .in14(1'b0), .in15(1'b0),
    .out(UnSigned_Overflow), .sel(AluOP));  // open: en
  Multiplexer #(.select(4), .width(32)) multiplexer_3 (
    .in0({32{1'b0}}), .in1({32{1'b0}}), .in2({32{1'b0}}), .in3(R21), .in4(R22), .in5({32{1'b0}}),
    .in6({32{1'b0}}), .in7({32{1'b0}}), .in8({32{1'b0}}), .in9({32{1'b0}}), .in10({32{1'b0}}),
    .in11({32{1'b0}}), .in12({32{1'b0}}), .in13({32{1'b0}}), .in14({32{1'b0}}), .in15({32{1'b0}}),
    .out(Result_2), .sel(AluOP));  // open: en
  Multiplexer #(.select(4)) multiplexer_4 (
    .in0(1'b0), .in1(1'b0), .in2(1'b0), .in3(1'b0), .in4(1'b0), .in5(OF1), .in6(OF2), .in7(1'b0), .in8(1'b0),
    .in9(1'b0), .in10(1'b0), .in11(1'b0), .in12(1'b0), .in13(1'b0), .in14(1'b0), .in15(1'b0),
    .out(Signed_Overflow), .sel(AluOP));  // open: en

  // Other names for the same wires on the sheet: OF = Signed_Overflow; Result2[31:0] = Result_2; S[3:0] = AluOP;
  //   UOF = UnSigned_Overflow

  // Notes on the sheet:
  //   不要改变此引脚区域内容，也不要改变ALU封装形式
  //   输入引脚
  //   请在下方利用上方输入输出引脚的隧道信号构建ALU电路，ctrl+d复制选择部件
  //   华中科技大学计算机学院 计算机组成原理，鸣谢加州大学伯克利CS61C课程
  //   输出引脚
  //   探测区域
endmodule

module PC (
  input  [31:0] in_1,
  input  [25:0] in_2,
  input  [15:0] in_3,
  input  [1:0] in_4,
  input  in_5,
  input  in_6,
  input  in_7,
  input  in_8,
  input  in_9,
  input  in_10,
  output [31:0] out_11,
  output [23:0] out_12,
  output [23:0] out_13,
  output [23:0] out_14,
  output [23:0] out_15,
  output [23:0] out_16
);

  wire and_2_out, and_3_out, and_4_out, and_5_out, and_6_out, incrementer_1_p1, JE, JN, JR, or_1_out,
       or_2_out, or_3_out;
  wire [1:1] and_1_out;
  wire [31:0] adder_1_out, incrementer_1_p2, multiplexer_1_out, multiplexer_2_out, multiplexer_3_out,
       multiplexer_4_out, PC_1, shifter_1_out, shifter_3_out, subtractor_1_out;
  wire [31:24] PC_q;

  Shifter #(.width(32), .shift("ar")) shifter_1 (.in({in_3, {16{1'b0}}}), .\dist (5'b01110), .out(shifter_1_out));
  Adder #(.width(32)) adder_1 (.a(out_11), .b(shifter_1_out), .out(adder_1_out));  // open: cin, cout
  Shifter #(.width(32), .shift("lr")) shifter_2 (.in(adder_1_out), .\dist (5'b00010));  // open: out
  Shifter #(.width(32), .shift("lr")) shifter_3 (.in(in_1), .\dist (5'b00010), .out(shifter_3_out));
  Multiplexer #(.width(32)) multiplexer_1 (
    .in0(PC_1), .in1(incrementer_1_p2), .out(multiplexer_1_out), .sel(in_5));  // open: en
  // Incrementer incrementer_1: pin names not known; wires that end beside it: incrementer_1_p1, incrementer_1_p2
  Multiplexer #(.width(32)) multiplexer_2 (
    .in0(incrementer_1_p2), .in1(PC_1), .out(multiplexer_2_out), .sel(in_5));  // open: en
  Multiplexer #(.select(2), .width(32)) multiplexer_3 (
    .in0(PC_1), .in1(shifter_3_out), .in2(multiplexer_1_out), .in3(multiplexer_2_out),
    .out(multiplexer_3_out), .sel(in_4));  // open: en
  Subtractor #(.width(32)) subtractor_1 (
    .a({{6{1'b0}}, in_2}), .b(32'hc00), .out(subtractor_1_out));  // open: bin, bout
  Multiplexer #(.select(2), .width(32)) multiplexer_4 (
    .in0(multiplexer_3_out), .in1(subtractor_1_out), .in2(incrementer_1_p2), .out(multiplexer_4_out),
    .sel({and_1_out[1], in_9}));  // open: in3, en
  and and_1 (and_1_out[1], in_1[31], in_10);
  Register #(.width(32)) PC (.D(multiplexer_4_out), .en(in_7), .Q({PC_q, out_12}), .clk(in_8), .clr(in_6));
  Shifter #(.width(32)) shifter_4 (.in({PC_q, out_12}), .\dist (5'b00010), .out(out_11));
  // Incrementer incrementer_2: pin names not known; wires that end beside it: {PC_q, out_12}, PC_1
  Decoder #(.select(2)) decoder_1 (.out1(JR), .out2(JE), .out3(JN), .sel(in_4));  // open: out0, en
  Counter #(.width(24), .max('hffffff)) counter_1 (
    .count(in_7), .Q(out_13), .clk(in_8), .clr(in_6));  // open: load, D, carry
  or or_1 (or_1_out, JN, JE);
  and and_2 (and_2_out, or_1_out, in_7);
  and and_3 (and_3_out, JN, ~in_5);  // AND_Gate
  and and_4 (and_4_out, in_5, JE);
  Counter #(.width(24), .max('hffffff)) counter_2 (
    .count(and_2_out), .Q(out_15), .clk(in_8), .clr(in_6));  // open: load, D, carry
  Counter #(.width(24), .max('hffffff)) counter_3 (
    .count(and_5_out), .Q(out_16), .clk(in_8), .clr(in_6));  // open: load, D, carry
  or or_2 (or_2_out, and_3_out, and_4_out);
  and and_5 (and_5_out, or_2_out, in_7);
  or or_3 (or_3_out, JR, in_9);
  Counter #(.width(24), .max('hffffff)) counter_4 (
    .count(and_6_out), .Q(out_14), .clk(in_8), .clr(in_6));  // open: load, D, carry
  and and_6 (and_6_out, or_3_out, in_7);

  // Other names for the same wires on the sheet: immi[15:0] = in_3; inst[25:0] = in_2; J = in_9; PC[23:0] = out_12;
  //   AluEq = in_5; BLTZ = in_10; EN = in_7; oPC[31:0] = out_11; PCW[1:0] = in_4; rS[31:0] = in_1; RST = in_6;
  //   T = in_8; 总周期数[23:0] = out_13; 无条件分支指令数[23:0] = out_14; 有条件分支成功跳转[23:0] = out_16; 有条件分支指令数[23:0] = out_15
endmodule

module Syscall (
  input  [31:0] in_1,
  input  [31:0] in_2,
  input  in_3,
  input  in_4,
  input  in_5,
  output out_6,
  output [31:0] out_7
);

  wire and_1_out, and_2_out, comparator_1_eq, or_1_out, register_2_q;
  wire [31:0] multiplexer_1_out;

  Comparator #(.width(32)) comparator_1 (.a(in_1), .b(32'ha), .eq(comparator_1_eq));  // open: gt, lt
  or or_1 (or_1_out, register_2_q, and_1_out);
  and and_1 (and_1_out, in_3, comparator_1_eq);
  and and_2 (and_2_out, ~comparator_1_eq, in_3);  // AND_Gate
  Register #(.width(32)) register_1 (.D(multiplexer_1_out), .Q(out_7), .clk(in_4), .clr(in_5));  // open: en
  Multiplexer #(.width(32)) multiplexer_1 (
    .in0(out_7), .in1(in_2), .out(multiplexer_1_out), .sel(and_2_out));  // open: en
  not not_1 (out_6, register_2_q);
  Register #(.width(1)) register_2 (.D(or_1_out), .Q(register_2_q), .clk(in_4), .clr(in_5));  // open: en

  // Other names for the same wires on the sheet: EN = out_6; rS[31:0] = in_1; RST = in_5; rT[31:0] = in_2; Sys = in_3;
  //   SyscallOut[31:0] = out_7; T = in_4
endmodule

module AluI (
  input  [1:0] in_1,
  input  [2:0] in_2,
  input  [31:0] in_3,
  input  [31:0] in_4,
  input  [31:0] in_5,
  input  [31:0] in_6,
  output [31:0] out_7,
  output [31:0] out_8
);

  wire [31:0] shifter_1_out;

  Shifter #(.width(32), .shift("ar")) shifter_1 (.in({in_3[15:0], {16{1'b0}}}), .\dist (5'b10000), .out(shifter_1_out));
  Multiplexer #(.select(2), .width(32)) multiplexer_1 (
    .in0(in_4), .in1(in_5), .in2(in_6), .out(out_7), .sel(in_1));  // open: in3, en
  Multiplexer #(.select(3), .width(32)) multiplexer_2 (
    .in0(in_5), .in1({{27{1'b0}}, in_3[10:6]}), .in2(shifter_1_out), .in3(32'h4), .in4(in_4), .out(out_8),
    .sel(in_2));  // open: in5, in6, in7, en

  // Other names for the same wires on the sheet: Instruction[31:0] = in_3; AluX[1:0] = in_1; AluY[2:0] = in_2;
  //   oPC[31:0] = in_6; rS[31:0] = in_4; rT[31:0] = in_5; X[31:0] = out_7; Y[31:0] = out_8

  // Notes on the sheet:
  //   Immi
  //   sa
endmodule
