// Logisim project alu-test.circ as structural Verilog: 3 circuits, main circuit main
module main (
  output Signed_Overflow,
  output Unsigned_overflow,
  output [31:0] Result,
  output Equal,
  output [31:0] Result_2
);

  wire clock_1_out;
  wire [3:0] rom_3_data;
  wire [7:0] adder_1_out, register_1_q;
  wire [31:0] rom_1_data, rom_2_data;

  Clock clock_1 (.out(clock_1_out));
  Adder adder_1 (.a(8'h1), .b(register_1_q), .out(adder_1_out));  // open: cin, cout
  Register register_1 (.D(adder_1_out), .Q(register_1_q), .clk(clock_1_out));  // open: en, clr
  // Probe on register_1_q
  // Probe on rom_1_data
  ROM #(.dataWidth(32)) rom_1 (.addr(register_1_q), .data(rom_1_data));  // open: sel
  ROM #(.dataWidth(32)) rom_2 (.addr(register_1_q), .data(rom_2_data));  // open: sel
  // Probe on rom_2_data
  ROM #(.dataWidth(4)) rom_3 (.addr(register_1_q), .data(rom_3_data));  // open: sel
  ALU alu_1 (
    .AluOP(rom_3_data), .X(rom_1_data), .Equal(Equal), .Result(Result), .Signed_Overflow(Signed_Overflow),
    .Y(rom_2_data), .Result_2(Result_2), .UnSigned_Overflow(Unsigned_overflow));
  // Probe on Result
  // Probe on Result_2

  // Notes on the sheet:
  //   此电路用于检测学生设计的ALU部件封装是否符合要求
  //   当电路设计完成后，蓝色线红色不应该出现，输出也不应该是高阻态
  //   ROM中可以存放测试用例，使用时钟驱动调出不同的X，Y，S值进行批量验证
  //   封装的ALU应该正好放置于此
endmodule

module test (
  input  [31:0] X,
  input  [31:0] Y,
  input  [3:0] ALUOP,
  output Signed_Overflow,
  output Unsigned_overflow,
  output [31:0] Result,
  output Equal,
  output [31:0] Result_2
);

  ALU alu_1 (
    .AluOP(ALUOP), .X(X), .Equal(Equal), .Result(Result), .Signed_Overflow(Signed_Overflow), .Y(Y),
    .Result_2(Result_2), .UnSigned_Overflow(Unsigned_overflow));

  // Notes on the sheet:
  //   封装的ALU应该正好放置于此
  //   此电路用于检测学生设计的ALU部件封装是否符合要求
  //   蓝色线红色不应该出现，输出也不应该是高阻态
endmodule

module my_alu_test_HuSixu (
  output Signed_Overflow,
  output Unsigned_overflow,
  output [31:0] Result,
  output Equal,
  output [31:0] Result_2
);

  wire and_1_out, clock_1_out, comparator_1_eq, comparator_2_eq, comparator_3_eq, comparator_4_eq,
       comparator_5_eq;
  wire [2:0] rom_4_data;
  wire [3:0] rom_3_data;
  wire [15:0] counter_1_q;
  wire [31:0] rom_1_data, rom_2_data, rom_5_data, rom_6_data;

  Clock clock_1 (.out(clock_1_out));
  Counter #(.width(16), .max('hffff)) counter_1 (
    .D({16{1'b1}}), .Q(counter_1_q), .clk(clock_1_out));  // open: load, count, carry, clr
  // Probe on counter_1_q
  // Probe on rom_1_data
  ROM #(.addrWidth(16), .dataWidth(32)) rom_1 (.addr(counter_1_q), .data(rom_1_data));  // open: sel
  ROM #(.addrWidth(16), .dataWidth(32)) rom_2 (.addr(counter_1_q), .data(rom_2_data));  // open: sel
  // Probe on rom_2_data
  ROM #(.addrWidth(16), .dataWidth(4)) rom_3 (.addr(counter_1_q), .data(rom_3_data));  // open: sel
  ROM #(.addrWidth(16), .dataWidth(3)) rom_4 (.addr(counter_1_q), .data(rom_4_data));  // open: sel
  ROM #(.addrWidth(16), .dataWidth(32)) rom_5 (.addr(counter_1_q), .data(rom_5_data));  // open: sel
  ROM #(.addrWidth(16), .dataWidth(32)) rom_6 (.addr(counter_1_q), .data(rom_6_data));  // open: sel
  ALU alu_1 (
    .AluOP(rom_3_data), .X(rom_1_data), .Equal(Equal), .Result(Result), .Signed_Overflow(Signed_Overflow),
    .Y(rom_2_data), .Result_2(Result_2), .UnSigned_Overflow(Unsigned_overflow));
  Comparator #(.width(1)) comparator_1 (.a(Signed_Overflow), .b(rom_4_data[0]), .eq(comparator_1_eq));  // open: gt, lt
  Comparator #(.width(1)) comparator_2 (
    .a(Unsigned_overflow), .b(rom_4_data[1]), .eq(comparator_2_eq));  // open: gt, lt
  Comparator #(.width(1)) comparator_3 (.a(Equal), .b(rom_4_data[2]), .eq(comparator_3_eq));  // open: gt, lt
  Comparator #(.width(32)) comparator_4 (.a(Result), .b(rom_5_data), .eq(comparator_4_eq));  // open: gt, lt
  Comparator #(.width(32)) comparator_5 (.a(Result_2), .b(rom_6_data), .eq(comparator_5_eq));  // open: gt, lt
  // Probe on Result
  // Probe on Result_2
  and and_1 (and_1_out, comparator_1_eq, comparator_2_eq, comparator_3_eq, comparator_4_eq, comparator_5_eq);
  LED Passed (.in(and_1_out));

  // Notes on the sheet:
  //   Expected Flags
  //   Expected Result
  //   Expected Result 2
  //   contents of rom_1 (hex, n*v repeats v):
  //   11111111 1231231 31231231 41adafdf
  //   封装的ALU应该正好放置于此
endmodule
